# Fritzing sketch stepper motor controller (saved by Fritzing 0.9.2b)
breadboards: 1

parts:
  Parte1 = Arduino Mega 2560 (Rev3)
  IC1 = ULN2803A [package=THT]
  M1 = Stepper Motor - Unipolar

nets:
  N1: Parte1.D11_PWM, IC1.In_4
  N2: Parte1.D10_PWM, IC1.In_3
  N3: Parte1.D9_PWM, IC1.In_2
  N4: Parte1.D8_PWM, IC1.In_1
  5V: Parte1.IOREF
  GND: IC1.0V
  N5: IC1.Out_4, M1.D
  N6: IC1.Out_3, M1.C
  N7: IC1.Out_2, M1.B
  N8: IC1.Out_1, M1.A
  12V: M1.COMMON_2
